// Logisim project two-bit-two-input-and.circ as structural Verilog: 1 circuit, main circuit main
module main (
  input  [1:0] in1,
  input  [1:0] in2,
  output [1:0] out
);

  assign out = in1 & in2;  // AND_Gate and_1, 2 bits wide
endmodule
