// Logisim project two-input-and-or.circ as structural Verilog: 2 circuits, main circuit main
module main (
  input  in1,
  input  in2,
  output out_3
);

  and and_1 (out_3, in1, in2);
endmodule

module _2nd_circuit (
  input  in1,
  input  in2,
  output out_3
);

  or or_1 (out_3, in1, in2);
endmodule
