// Logisim project two-input-and-with-constant-input.circ as structural Verilog: 1 circuit, main circuit main
module main (
);

  wire and_1_out;

  and and_1 (and_1_out, 1'b1, 1'b1);
  // also tied to VCC on the sheet: and_1_out
endmodule
